// Logisim project ukol_adder4.circ as structural Verilog: 2 circuits, main circuit adder1
module adder1 (
  input  A,
  input  B,
  input  Cin,
  output S,
  output Cout
);

  wire and_1_out, and_2_out, xor_1_out;

  xor xor_1 (xor_1_out, A, B);
  xor xor_2 (S, xor_1_out, Cin);
  and and_1 (and_1_out, xor_1_out, Cin);
  and and_2 (and_2_out, A, B);
  or or_1 (Cout, and_1_out, and_2_out);
endmodule

module adder4 (
  input  in_1,
  input  in_2,
  input  in_3,
  input  in_4,
  input  in_5,
  input  in_6,
  input  in_7,
  input  in_8,
  input  in_9,
  output out_10,
  output out_11,
  output out_12,
  output out_13,
  output out_14
);

  wire adder1_1_cout, adder1_2_cout, adder1_3_cout;

  adder1 adder1_1 (.A(in_1), .B(in_2), .Cin(in_3), .S(out_10), .Cout(adder1_1_cout));
  adder1 adder1_2 (.A(in_4), .B(in_5), .Cin(adder1_1_cout), .S(out_11), .Cout(adder1_2_cout));
  adder1 adder1_3 (.A(in_6), .B(in_7), .Cin(adder1_2_cout), .S(out_12), .Cout(adder1_3_cout));
  adder1 adder1_4 (.A(in_8), .B(in_9), .Cin(adder1_3_cout), .S(out_13), .Cout(out_14));
endmodule
