// Logisim project ukol_multi_and_sevseg_and_adder.circ as structural Verilog
module segmg (
  input  d,
  input  c,
  input  b,
  input  a,
  output sa,
  output sb,
  output sc,
  output sd,
  output se,
  output sf,
  output sg
);

  wire and_1_out, and_2_out, and_3_out, and_4_out, and_5_out, and_6_out, and_7_out, and_8_out, and_9_out,
       and_10_out, and_11_out, and_12_out, and_13_out, and_14_out, and_15_out, and_16_out, and_17_out,
       and_18_out, not_1_out, not_2_out, not_3_out, not_4_out;

  not not_1 (not_1_out, d);
  not not_2 (not_2_out, c);
  not not_3 (not_3_out, b);
  not not_4 (not_4_out, a);
  and and_1 (and_1_out, not_4_out, not_2_out);
  and and_2 (and_2_out, a, c);
  and and_3 (and_3_out, not_4_out, not_3_out);
  and and_4 (and_4_out, a, b);
  and and_5 (and_5_out, not_2_out, not_1_out);
  and and_6 (and_6_out, not_1_out, c);
  and and_7 (and_7_out, not_4_out, not_2_out);
  and and_8 (and_8_out, a, not_3_out, c);
  and and_9 (and_9_out, b, not_2_out, not_1_out);
  and and_10 (and_10_out, b, not_4_out);
  and and_11 (and_11_out, not_4_out, not_2_out);
  and and_12 (and_12_out, b, not_4_out);
  and and_13 (and_13_out, not_4_out, not_3_out);
  and and_14 (and_14_out, c, not_4_out, b);
  and and_15 (and_15_out, c, not_3_out, not_1_out);
  and and_16 (and_16_out, b, not_2_out, not_1_out);
  and and_17 (and_17_out, c, not_1_out, not_3_out);
  and and_18 (and_18_out, b, not_4_out);
  or or_1 (sa, d, b, and_1_out, and_2_out);
  or or_2 (sb, d, and_3_out, and_4_out, and_5_out);
  or or_3 (sc, a, not_3_out, and_6_out);
  or or_4 (sd, and_7_out, and_8_out, and_9_out, and_10_out, d);
  or or_5 (se, and_11_out, and_12_out);
  or or_6 (sf, and_13_out, d, and_14_out, and_15_out);
  or or_7 (sg, and_16_out, and_17_out, and_18_out, d);
endmodule

module zobrazeni (
  input  a,
  input  b,
  input  c,
  input  d
);

  wire segmg_1_sa, segmg_1_sb, segmg_1_sc, segmg_1_sd, segmg_1_se, segmg_1_sf, segmg_1_sg;

  segmg segmg_1 (
    .d(a), .c(b), .b(c), .a(d), .sa(segmg_1_sa), .sb(segmg_1_sb), .sc(segmg_1_sc), .sd(segmg_1_sd),
    .se(segmg_1_se), .sf(segmg_1_sf), .sg(segmg_1_sg));
  _7_Segment_Display u_7_segment_display_1 (
    .g(segmg_1_sg), .f(segmg_1_sf), .a(segmg_1_sa), .b(segmg_1_sb), .e(segmg_1_se), .d(segmg_1_sd),
    .c(segmg_1_sc));  // open: dp
endmodule

module multi (
  input  a1,
  input  a0,
  input  b1,
  input  b0,
  output s3,
  output s2,
  output s1,
  output s0
);

  wire and_2_out, and_3_out, and_4_out, and_5_out, and_6_out, and_7_out, not_1_out, not_2_out, not_3_out,
       not_4_out;

  not not_1 (not_1_out, a1);
  not not_2 (not_2_out, a0);
  not not_3 (not_3_out, b1);
  not not_4 (not_4_out, b0);
  and and_1 (s3, b1, b0, a1, a0);
  and and_2 (and_2_out, b1, not_4_out, a1);
  and and_3 (and_3_out, b1, a1, not_2_out);
  and and_4 (and_4_out, a1, b0, not_3_out);
  and and_5 (and_5_out, b0, a1, not_2_out);
  and and_6 (and_6_out, b1, not_1_out, a0);
  and and_7 (and_7_out, b1, a0, not_4_out);
  and and_8 (s0, b0, a0);
  or or_1 (s2, and_2_out, and_3_out);
  or or_2 (s1, and_4_out, and_5_out, and_6_out, and_7_out);
endmodule

module zobrazeniMulti (
  input  in_1,
  input  in_2,
  input  in_3,
  input  in_4
);

  wire multi_1_s0, multi_1_s1, multi_1_s2, multi_1_s3, segmg_1_sa, segmg_1_sb, segmg_1_sc, segmg_1_sd,
       segmg_1_se, segmg_1_sf, segmg_1_sg;

  multi multi_1 (
    .a1(in_1), .a0(in_2), .b1(in_3), .b0(in_4), .s3(multi_1_s3), .s2(multi_1_s2), .s1(multi_1_s1),
    .s0(multi_1_s0));
  segmg segmg_1 (
    .d(multi_1_s3), .c(multi_1_s2), .b(multi_1_s1), .a(multi_1_s0), .sa(segmg_1_sa), .sb(segmg_1_sb),
    .sc(segmg_1_sc), .sd(segmg_1_sd), .se(segmg_1_se), .sf(segmg_1_sf), .sg(segmg_1_sg));
  _7_Segment_Display u_7_segment_display_1 (
    .g(segmg_1_sg), .f(segmg_1_sf), .a(segmg_1_sa), .b(segmg_1_sb), .e(segmg_1_se), .d(segmg_1_sd),
    .c(segmg_1_sc));  // open: dp
endmodule
